# Fritzing sketch lighting_schematic (saved by Fritzing 0.9.3b)
breadboards: 1

parts:
  Part1 = Arduino Uno (Rev3)
  KY-1 = Keyes Relay [package=THT]
  Part2 = Adafruit DS3231 [part_number="Adafruit #3013"]
  S1 = Pushbutton [package="[THT]"]
  R1 = Resistor [tolerance=±5% resistance=10k package=THT]
  LED1 = LED - 5mm [color="Red (633nm)" package="5 mm [THT]"]
  J1 = Screw terminal - 2 pins [package=THT]

nets:
  N1: Part1.A4/SDA, Part2.SDA
  N2: Part1.A5/SCL, Part2.SCL
  N3: Part1.D6_PWM, S1.Pin_1, S1.Pin_2, R1.Pin_0
  N4: Part1.D7, KY-1.signal
  5V: Part1.5V, KY-1.power, Part2.Vin, S1.Pin_3, S1.Pin_4
  GND: Part1.GND, KY-1.ground, Part2.GND, R1.Pin_1
  N5: KY-1.C, J1.pin1
  N6: KY-1.NO, LED1.anode
  N7: LED1.cathode, J1.pin2

notes:
  LED driver
  wall outlet

custom parts:
  Keyes Relay: The Keyes 5V relay module is suitable for SCM development, home appliance control. It uses a 5V~12V TIL control signal which can control DC / AC signal.
  Adafruit DS3231: The datasheet for the DS3231 explains that this part is an "Extremely Accurate I²C-Integrated RTC/TCXO/Crystal". And, hey, it does exactly what it says on the tin! This Real Time Clock (RTC) is the most precise you can get in a small, low power package. Most RTCs use an external 32kHz timing crystal that is used to keep time with low current draw. And that's all well and good, but those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
